// Logisim project ALU.circ as structural Verilog: 1 circuit, main circuit ALU
module ALU (
  input  add,
  input  \and ,
  input  mult,
  input  addi,
  input  andi,
  input  mulu,
  input  sub,
  input  \or ,
  input  [31:0] Data_A,
  input  ori,
  input  div,
  input  slt,
  input  slti,
  input  \nor ,
  input  divu,
  input  [31:0] Data_B,
  input  sltu,
  input  \xor ,
  input  sltui,
  input  xori,
  output [31:0] ALU_Output,
  output [31:0] High,
  output Zero_Flag,
  output Negative_Flag
);

  wire _0, _1, _2, _3, add_t_t, and_t_t, or_t_t, slt_bit, slt_t, sltu_bit, sltu_t, xor_t_t;
  wire [1:0] MiniSelector;
  wire [31:0] Add_t, And_t, DivHigh, DivLow, DivuHigh, DivuLow, Low, MultHigh, MultLow, MuluHigh, MuluLow,
       Nor_t, Operations, Or_t, slt_32, sltu_32, Sub_t, Xor_t;

  Sig_Mul sig_mul_1 (.A(Data_A), .B(Data_B), .Low(MultLow), .High(MultHigh));
  Multiplexer #(.select(3), .width(32), .enable("false")) multiplexer_1 (
    .in0(Add_t), .in1(Sub_t), .in2(slt_32), .in3(sltu_32), .in4(And_t), .in5(Or_t), .in6(Nor_t), .in7(Xor_t),
    .out(Operations), .sel({_2, _1, _0}));
  Adder #(.width(32)) adder_1 (.a(Data_A), .b(Data_B), .out(Add_t));  // open: cin, cout
  Multiplier #(.width(32)) multiplier_1 (.a(Data_A), .b(Data_B), .out(MuluLow), .cout(MuluHigh));  // open: cin
  Comparator #(.width(32)) comparator_1 (.a(Data_A), .b(Data_B), .lt(slt_bit));  // open: gt, eq
  assign slt_32 = {{31{1'b0}}, slt_bit};  // Bit_Extender bit_extender_1
  Multiplexer #(.select(2), .width(32), .enable("false")) multiplexer_2 (
    .in0(MultHigh), .in1(DivHigh), .in2(MuluHigh), .in3(DivuHigh), .out(High), .sel(MiniSelector));
  or or_1 (MiniSelector[0], _1, _2);
  or or_2 (MiniSelector[1], _0, _2);
  Subtractor #(.width(32)) subtractor_1 (.a(Data_A), .b(Data_B), .out(Sub_t));  // open: bin, bout
  Divider #(.width(32)) divider_1 (.a(Data_A), .b(Data_B), .out(DivuLow), .rem(DivuHigh));  // open: upper
  Sig_DIV sig_div_1 (.A(Data_A), .B(Data_B), .Low(DivLow), .High(DivHigh));
  Comparator #(.width(32), .mode("unsigned")) comparator_2 (.a(Data_A), .b(Data_B), .lt(sltu_bit));  // open: gt, eq
  assign sltu_32 = {{31{1'b0}}, sltu_bit};  // Bit_Extender bit_extender_2
  Multiplexer #(.width(32), .enable("false")) multiplexer_3 (.in0(Operations), .in1(Low), .out(ALU_Output), .sel(_3));
  Multiplexer #(.select(2), .width(32), .enable("false")) multiplexer_4 (
    .in0(MultLow), .in1(DivLow), .in2(MuluLow), .in3(DivuLow), .out(Low), .sel(MiniSelector));
  assign And_t = Data_A & Data_B;  // AND_Gate and_1, 32 bits wide
  assign Or_t = Data_A | Data_B;  // OR_Gate or_3, 32 bits wide
  Comparator #(.width(32)) comparator_3 (
    .a(ALU_Output), .b({32{1'b0}}), .eq(Zero_Flag), .lt(Negative_Flag));  // open: gt
  assign Nor_t = ~(Data_A | Data_B);  // NOR_Gate nor_1, 32 bits wide
  assign Xor_t = Data_A ^ Data_B;  // XOR_Gate xor_1, 32 bits wide
  or or_4 (add_t_t, add, addi);
  or or_5 (slt_t, slt, slti);
  or or_6 (sltu_t, sltu, sltui);
  or or_7 (_0, sub, sltu_t, xor_t_t, or_t_t, mulu);
  or or_8 (_1, slt_t, sltu_t, \nor , xor_t_t, div);
  or or_9 (and_t_t, \and , andi);
  or or_10 (or_t_t, \or , ori);
  or or_11 (xor_t_t, \xor , xori);
  or or_12 (_2, and_t_t, or_t_t, \nor , xor_t_t, divu);
  or or_13 (_3, mult, mulu, div, divu);

  // Other names for the same wires on the sheet: A[31:0] = Data_A; B[31:0] = Data_B;
  //   OP_Selector[3:0] = {_3, _2, _1, _0}; Selector[2:0] = {_2, _1, _0}; Enable = _3; Output[31:0] = ALU_Output;
  //   sltiu = sltui

  // Notes on the sheet:
  //   INPUTS
  //   ARITHMETIC
  //   OUTPUTS
  //   LOGIC
  //   Operations
endmodule
