// Logisim project Control Unit.circ as structural Verilog: 1 circuit, main circuit Control Unit
module Control_Unit (
  input  Read_RAM,
  input  Clock,
  input  Reset,
  input  Write_RAM,
  input  halt,
  input  [3:0] Read_RAM_time,
  input  [3:0] Write_RAM_time,
  output E_inst,
  output CS,
  output Read_End,
  output R_W,
  output E_PC,
  output End,
  output PC_Address
);

  wire chip_1, chip_2, crono_1_finish, crono_2_finish, crono_rst_1, crono_rst_2, demultiplexer_1_out1,
       demultiplexer_2_out0, demultiplexer_3_out0, demultiplexer_4_out0, demultiplexer_4_out1,
       demultiplexer_5_out0, IDLE_q, Load_Inst_q, or_2_out, or_3_out, or_5_out, or_8_out, RAM, RAM_read_load;
  wire [3:0] multiplexer_1_out;

  or or_1 (E_PC, demultiplexer_5_out0, RAM_read_load);
  Multiplexer #(.width(4), .enable("false")) multiplexer_1 (
    .in0(Read_RAM_time), .in1(Write_RAM_time), .out(multiplexer_1_out), .sel(Write_RAM));
  or or_2 (or_2_out, demultiplexer_5_out0, RAM_read_load, demultiplexer_1_out1);
  D_Flip_Flop d_ff_1 (.clk(Clock), .D(or_3_out), .Q(chip_2), .reset(Reset));  // open: Qn, preset, en
  or or_3 (or_3_out, demultiplexer_2_out0, crono_rst_2);
  D_Flip_Flop IDLE (.clk(Clock), .D(or_2_out), .Q(IDLE_q), .preset(Reset));  // open: Qn, en, reset
  Demultiplexer #(.enable("false")) demultiplexer_1 (
    .out0(crono_rst_1), .out1(demultiplexer_1_out1), .in(IDLE_q), .sel(Reset));
  Demultiplexer #(.enable("false")) demultiplexer_2 (
    .out0(demultiplexer_2_out0), .out1(Read_End), .in(chip_2), .sel(crono_1_finish));
  Crono crono_1 (.Time(multiplexer_1_out), .reset(crono_rst_2), .clock(Clock), .finish(crono_1_finish));
  or or_4 (RAM, Read_RAM, Write_RAM);
  or or_5 (or_5_out, demultiplexer_3_out0, crono_rst_1);
  D_Flip_Flop Load_Read (.clk(Clock), .D(Read_End), .Q(RAM_read_load), .reset(Reset));  // open: Qn, preset, en
  D_Flip_Flop Read_Inst (.clk(Clock), .D(or_5_out), .Q(chip_1), .reset(Reset));  // open: Qn, preset, en
  Crono crono_2 (.Time(Read_RAM_time), .reset(crono_rst_1), .clock(Clock), .finish(crono_2_finish));
  or or_6 (CS, chip_1, chip_2);
  Demultiplexer #(.enable("false")) demultiplexer_3 (
    .out0(demultiplexer_3_out0), .out1(E_inst), .in(chip_1), .sel(crono_2_finish));
  or or_7 (PC_Address, chip_1, crono_rst_1, E_PC);
  D_Flip_Flop Load_Inst (.clk(Clock), .D(E_inst), .Q(Load_Inst_q), .reset(Reset));  // open: Qn, preset, en
  Demultiplexer #(.enable("false")) demultiplexer_4 (
    .out0(demultiplexer_4_out0), .out1(demultiplexer_4_out1), .in(Load_Inst_q), .sel(halt));
  Demultiplexer #(.enable("false")) demultiplexer_5 (
    .out0(demultiplexer_5_out0), .out1(crono_rst_2), .in(demultiplexer_4_out0), .sel(RAM));
  or or_8 (or_8_out, demultiplexer_4_out1, End);
  D_Flip_Flop u_Halt (.clk(Clock), .D(or_8_out), .Q(End), .reset(Reset));  // open: Qn, preset, en
  and and_1 (R_W, Write_RAM, chip_2);

  // Other names for the same wires on the sheet: clk = Clock; R_W_t = crono_rst_2; R_W_RAM = R_W;
  //   Read_time[3:0] = Read_RAM_time; rst = Reset; Write_time[3:0] = Write_RAM_time

  // Notes on the sheet:
  //   Inputs
  //   Outputs
endmodule
