// Logisim project Crono.circ as structural Verilog: 1 circuit, main circuit Crono
module Crono (
  input  [3:0] Time,
  input  reset,
  input  clock,
  output finish
);

  wire [3:0] counter_1_q;

  Counter #(.width(4), .max('hf)) counter_1 (
    .count(1'b1), .Q(counter_1_q), .clk(clock), .clr(reset));  // open: load, D, carry
  Comparator #(.width(4)) comparator_1 (.a(Time), .b(counter_1_q), .eq(finish));  // open: gt, lt

  // Other names for the same wires on the sheet: clk = clock; rst = reset

  // Notes on the sheet:
  //   Inputs
  //   Output
endmodule
