// Logisim project Data Path.circ as structural Verilog: 1 circuit, main circuit Data Path
module Data_Path (
  input  Clock,
  input  add,
  input  mflo,
  input  divu,
  input  Type_I,
  input  [31:0] Instruction,
  input  [25:0] jump,
  input  sub,
  input  addi,
  input  sltiu,
  input  Reset,
  input  \and ,
  input  andi,
  input  ori,
  input  E_PC,
  input  [15:0] cte,
  input  [31:0] B_C,
  input  \or ,
  input  rnd,
  input  xori,
  input  Read_end,
  input  \nor ,
  input  kbd,
  input  sw,
  input  [4:0] Rs,
  input  E_inst,
  input  \xor ,
  input  slti,
  input  push,
  input  [6:0] Keyboard,
  input  [4:0] Rt,
  input  slt,
  input  mult,
  input  lw,
  input  KBD_AVAIL,
  input  sltu,
  input  mulu,
  input  pop,
  input  [4:0] Rd,
  input  PC_Address,
  input  mfhi,
  input  div,
  input  tty,
  output [31:0] Dir_Address,
  output [31:0] RAM__w,
  output Read_RAM,
  output kbd_2,
  output Write_RAM,
  output tty_2,
  output [6:0] tty_DATA,
  output [31:0] Rs_2,
  output [31:0] PC,
  output [31:0] Rt_2
);

  wire and_1_out, and_2_out, E_HL, Neg, or_1_out, or_2_out, or_3_out, or_4_out, or_5_out, or_7_out, or_8_out,
       or_10_out, R_W, Zero;
  wire [4:0] multiplexer_3_out;
  wire [31:0] ALU_Output, bit_extender_2_out, cte_I15, Hi, High, in_register_file_1_rf_input, Lo,
       multiplexer_1_out, multiplexer_2_out, SP;

  or or_1 (or_1_out, add, sub, \and , \or );
  or or_2 (or_2_out, \nor , \xor , slt, sltu);
  or or_3 (or_3_out, mfhi, mflo, addi, andi);
  or or_4 (or_4_out, slti, ori, xori, sltiu);
  or or_5 (or_5_out, rnd, kbd, E_HL);
  or or_6 (E_HL, mult, mulu, div, divu);
  or or_7 (or_7_out, or_1_out, or_2_out, or_3_out, or_4_out, or_5_out);
  and and_1 (and_1_out, E_PC, or_7_out);
  or or_8 (or_8_out, lw, pop);
  and and_2 (and_2_out, or_8_out, Read_end);
  assign cte_I15 = {{16{cte[15]}}, cte};  // Bit_Extender bit_extender_1
  assign bit_extender_2_out = {{16{1'b0}}, cte};  // Bit_Extender bit_extender_2
  or or_9 (R_W, and_1_out, and_2_out);
  Multiplexer #(.width(32), .enable("false")) multiplexer_1 (
    .in0(cte_I15), .in1(bit_extender_2_out), .out(multiplexer_1_out), .sel(or_10_out));
  or or_10 (or_10_out, andi, ori, xori);
  Multiplexer #(.width(32), .enable("false")) multiplexer_2 (
    .in0(Rt_2), .in1(multiplexer_1_out), .out(multiplexer_2_out), .sel(Type_I));
  In_Register_File in_register_file_1 (
    .rnd(rnd), .RAM(Instruction), .kbd(kbd), .mfhi(mfhi), .ALU_Output(ALU_Output), .mflo(mflo), .pop(pop),
    .Keyboard(Keyboard), .lw(lw), .Clock(Clock), .High(Hi), .KBD_AVAIL(KBD_AVAIL), .Low(Lo),
    .RF_Input(in_register_file_1_rf_input));
  ALU alu_1 (
    .add(add), .\and (\and ), .mult(mult), .addi(addi), .andi(andi), .mulu(mulu), .sub(sub), .\or (\or ),
    .Data_A(Rs_2), .ori(ori), .div(div), .slt(slt), .slti(slti), .\nor (\nor ), .divu(divu),
    .Data_B(multiplexer_2_out), .sltu(sltu), .\xor (\xor ), .sltui(sltiu), .xori(xori),
    .ALU_Output(ALU_Output), .High(High), .Zero_Flag(Zero), .Negative_Flag(Neg));
  PC pc_1 (.Branch_Control(B_C), .Instruction(PC), .Enabled(E_PC), .Clock(Clock), .Reset(Reset));
  Multiplexer #(.width(5), .enable("false")) multiplexer_3 (.in0(Rd), .in1(Rt), .out(multiplexer_3_out), .sel(Type_I));
  Register_File register_file_1 (
    .Data_Address(multiplexer_3_out), .Data_In(in_register_file_1_rf_input), .Output_A(Rs_2), .High(High),
    .R_W(R_W), .Read_A(Rs), .Read_B(Rt), .Clock(Clock), .Reset(Reset), .E_HL(E_HL), .Output_B(Rt_2),
    .push(push), .pop(pop), .E_PC(E_PC), .High_2(Hi), .Low(Lo), .SP(SP));
  or or_11 (Write_RAM, sw, push);
  Multiplexer #(.width(32), .enable("false")) multiplexer_4 (.in0(Rs_2), .in1(Rt_2), .out(RAM__w), .sel(sw));
  and and_3 (tty_2, tty, E_PC);
  or or_12 (Read_RAM, lw, pop);
  Ram_Address ram_address_1 (
    .ALU(ALU_Output), .SP(SP), .PC(PC), .sw(sw), .lw(lw), .pop(pop), .push(push), .PC_Address(PC_Address),
    .Dir_RAM(Dir_Address));

  assign kbd_2 = kbd;
  assign tty_DATA = Rs_2[6:0];

  // Other names for the same wires on the sheet: Clk = Clock; Read__RAM = Read_RAM; Rs_t[31:0] = Rs_2; Rst = Reset;
  //   Rt_t[31:0] = Rt_2

  // Notes on the sheet:
  //   Inputs
  //   Outputs
endmodule
