// Logisim project ID.circ as structural Verilog: 1 circuit, main circuit ID
module ID (
  input  [31:0] Instruction,
  output [25:0] jump,
  output [15:0] cte,
  output [4:0] Rs,
  output add,
  output \nor ,
  output pop,
  output push,
  output halt,
  output rnd,
  output addi,
  output beq,
  output j,
  output [4:0] Rt,
  output sub,
  output \xor ,
  output tty,
  output kbd,
  output andi,
  output bne,
  output [4:0] Rd,
  output mult,
  output slt,
  output ori,
  output blez,
  output mulu,
  output sltu,
  output xori,
  output bgtz,
  output Tyoe_I,
  output div,
  output mfhi,
  output slti,
  output bltz,
  output divu,
  output mflo,
  output sltiu,
  output lw,
  output \and ,
  output nop,
  output sw,
  output \or ,
  output jr
);

  wire _00_0000, _11_1000, _11_1111, comparator_5_eq, comparator_6_eq, comparator_7_eq, comparator_8_eq,
       comparator_13_eq, comparator_14_eq, comparator_15_eq, comparator_16_eq, comparator_22_eq,
       comparator_23_eq, comparator_24_eq, comparator_25_eq, comparator_30_eq, comparator_31_eq,
       comparator_32_eq, comparator_33_eq, comparator_34_eq, comparator_35_eq, comparator_36_eq,
       comparator_37_eq, comparator_38_eq, comparator_39_eq, or_1_out, or_2_out, or_3_out;

  Comparator #(.width(6)) comparator_1 (.a(Instruction[31:26]), .b({6{1'b0}}), .eq(_00_0000));  // open: gt, lt
  Comparator #(.width(6)) comparator_2 (.a(Instruction[31:26]), .b(6'b001000), .eq(addi));  // open: gt, lt
  Comparator #(.width(6)) comparator_3 (.a(Instruction[31:26]), .b(6'b001010), .eq(slti));  // open: gt, lt
  Comparator #(.width(6)) comparator_4 (.a(Instruction[31:26]), .b(6'b000110), .eq(blez));  // open: gt, lt
  Comparator #(.width(6)) comparator_5 (.a(Instruction[5:0]), .b(6'b100000), .eq(comparator_5_eq));  // open: gt, lt
  Comparator #(.width(6)) comparator_6 (.a(Instruction[5:0]), .b(6'b011010), .eq(comparator_6_eq));  // open: gt, lt
  Comparator #(.width(6)) comparator_7 (.a(Instruction[5:0]), .b(6'b100111), .eq(comparator_7_eq));  // open: gt, lt
  Comparator #(.width(6)) comparator_8 (.a(Instruction[5:0]), .b(6'b010000), .eq(comparator_8_eq));  // open: gt, lt
  and and_1 (add, _00_0000, comparator_5_eq);
  and and_2 (div, _00_0000, comparator_6_eq);
  and and_3 (\nor , _00_0000, comparator_7_eq);
  and and_4 (mfhi, _00_0000, comparator_8_eq);
  Comparator #(.width(6)) comparator_9 (.a(Instruction[31:26]), .b(6'b111000), .eq(_11_1000));  // open: gt, lt
  Comparator #(.width(6)) comparator_10 (.a(Instruction[31:26]), .b(6'b001100), .eq(andi));  // open: gt, lt
  Comparator #(.width(6)) comparator_11 (.a(Instruction[31:26]), .b(6'b001011), .eq(sltiu));  // open: gt, lt
  Comparator #(.width(6)) comparator_12 (.a(Instruction[31:26]), .b(6'b000111), .eq(bgtz));  // open: gt, lt
  Comparator #(.width(6)) comparator_13 (.a(Instruction[5:0]), .b(6'b100010), .eq(comparator_13_eq));  // open: gt, lt
  Comparator #(.width(6)) comparator_14 (.a(Instruction[5:0]), .b(6'b011011), .eq(comparator_14_eq));  // open: gt, lt
  Comparator #(.width(6)) comparator_15 (.a(Instruction[5:0]), .b(6'b101000), .eq(comparator_15_eq));  // open: gt, lt
  Comparator #(.width(6)) comparator_16 (.a(Instruction[5:0]), .b(6'b010010), .eq(comparator_16_eq));  // open: gt, lt
  Comparator #(.width(6)) comparator_17 (.a(Instruction[31:26]), .b(6'b101011), .eq(sw));  // open: gt, lt
  and and_5 (sub, _00_0000, comparator_13_eq);
  and and_6 (divu, _00_0000, comparator_14_eq);
  and and_7 (\xor , _00_0000, comparator_15_eq);
  and and_8 (mflo, _00_0000, comparator_16_eq);
  Comparator #(.width(6)) comparator_18 (.a(Instruction[31:26]), .b({6{1'b1}}), .eq(_11_1111));  // open: gt, lt
  Comparator #(.width(6)) comparator_19 (.a(Instruction[31:26]), .b(6'b001101), .eq(ori));  // open: gt, lt
  Comparator #(.width(6)) comparator_20 (.a(Instruction[31:26]), .b(6'b000100), .eq(beq));  // open: gt, lt
  Comparator #(.width(6)) comparator_21 (.a(Instruction[31:26]), .b(6'b000001), .eq(bltz));  // open: gt, lt
  Comparator #(.width(6)) comparator_22 (.a(Instruction[5:0]), .b(6'b011000), .eq(comparator_22_eq));  // open: gt, lt
  Comparator #(.width(6)) comparator_23 (.a(Instruction[5:0]), .b(6'b100100), .eq(comparator_23_eq));  // open: gt, lt
  Comparator #(.width(6)) comparator_24 (.a(Instruction[5:0]), .b(6'b101010), .eq(comparator_24_eq));  // open: gt, lt
  Comparator #(.width(6)) comparator_25 (.a(Instruction[5:0]), .b({6{1'b0}}), .eq(comparator_25_eq));  // open: gt, lt
  and and_9 (mult, _00_0000, comparator_22_eq);
  and and_10 (\and , _00_0000, comparator_23_eq);
  and and_11 (slt, _00_0000, comparator_24_eq);
  and and_12 (nop, _00_0000, comparator_25_eq);
  Comparator #(.width(6)) comparator_26 (.a(Instruction[31:26]), .b(6'b000010), .eq(j));  // open: gt, lt
  Comparator #(.width(6)) comparator_27 (.a(Instruction[31:26]), .b(6'b001110), .eq(xori));  // open: gt, lt
  Comparator #(.width(6)) comparator_28 (.a(Instruction[31:26]), .b(6'b000101), .eq(bne));  // open: gt, lt
  Comparator #(.width(6)) comparator_29 (.a(Instruction[31:26]), .b(6'b100011), .eq(lw));  // open: gt, lt
  and and_13 (mulu, _00_0000, comparator_30_eq);
  Comparator #(.width(6)) comparator_30 (.a(Instruction[5:0]), .b(6'b011001), .eq(comparator_30_eq));  // open: gt, lt
  and and_14 (\or , _00_0000, comparator_31_eq);
  Comparator #(.width(6)) comparator_31 (.a(Instruction[5:0]), .b(6'b100101), .eq(comparator_31_eq));  // open: gt, lt
  and and_15 (sltu, _00_0000, comparator_32_eq);
  Comparator #(.width(6)) comparator_32 (.a(Instruction[5:0]), .b(6'b101011), .eq(comparator_32_eq));  // open: gt, lt
  and and_16 (jr, _00_0000, comparator_33_eq);
  Comparator #(.width(6)) comparator_33 (.a(Instruction[5:0]), .b(6'b001000), .eq(comparator_33_eq));  // open: gt, lt
  or or_1 (or_1_out, addi, andi, ori, xori, slti);
  or or_2 (or_2_out, sltiu, beq, bne);
  or or_3 (or_3_out, blez, bgtz, bltz, lw, sw);
  or or_4 (Tyoe_I, or_1_out, or_2_out, or_3_out);
  Comparator #(.width(6)) comparator_34 (.a(Instruction[5:0]), .b({6{1'b0}}), .eq(comparator_34_eq));  // open: gt, lt
  Comparator #(.width(6)) comparator_35 (.a(Instruction[5:0]), .b(6'b000001), .eq(comparator_35_eq));  // open: gt, lt
  Comparator #(.width(6)) comparator_36 (.a(Instruction[5:0]), .b({6{1'b1}}), .eq(comparator_36_eq));  // open: gt, lt
  Comparator #(.width(6)) comparator_37 (.a(Instruction[5:0]), .b(6'b000001), .eq(comparator_37_eq));  // open: gt, lt
  Comparator #(.width(6)) comparator_38 (.a(Instruction[5:0]), .b(6'b000010), .eq(comparator_38_eq));  // open: gt, lt
  Comparator #(.width(6)) comparator_39 (.a(Instruction[5:0]), .b(6'b000100), .eq(comparator_39_eq));  // open: gt, lt
  and and_17 (pop, comparator_34_eq, _11_1000);
  and and_18 (push, _11_1000, comparator_35_eq);
  and and_19 (halt, _11_1111, comparator_36_eq);
  and and_20 (tty, _11_1111, comparator_37_eq);
  and and_21 (rnd, _11_1111, comparator_38_eq);
  and and_22 (kbd, _11_1111, comparator_39_eq);

  assign cte = Instruction[15:0];
  assign jump = Instruction[25:0];
  assign Rd = Instruction[15:11];
  assign Rs = Instruction[25:21];
  assign Rt = Instruction[20:16];

  // Other names for the same wires on the sheet: func__code[5:0] = Instruction[5:0];
  //   op__code[5:0] = Instruction[31:26]

  // Notes on the sheet:
  //   op. code: 00 0000
  //   Type R 
  //   op. code: 11 1000
  //   op. code: 11 1111
  //   Type I
  //   --------
  //   Type J
  //   --------
endmodule
