// Logisim project In Register File.circ as structural Verilog: 1 circuit, main circuit In-Register File
module In_Register_File (
  input  rnd,
  input  [31:0] RAM,
  input  kbd,
  input  mfhi,
  input  [31:0] ALU_Output,
  input  mflo,
  input  pop,
  input  [6:0] Keyboard,
  input  lw,
  input  Clock,
  input  [31:0] High,
  input  KBD_AVAIL,
  input  [31:0] Low,
  output [31:0] RF_Input
);

  wire ram_t;
  wire [2:0] selector;
  wire [31:0] KBD_in, KBD_t, random;

  Random #(.width(32)) u_Rnd (.clk(Clock), .next(rnd), .out(random));  // open: clr
  assign KBD_t = {{25{1'b0}}, Keyboard};  // Bit_Extender bit_extender_1
  or or_1 (ram_t, pop, lw);
  or or_2 (selector[0], kbd, ram_t, mflo);
  or or_3 (selector[1], rnd, ram_t);
  or or_4 (selector[2], mfhi, mflo);
  Multiplexer #(.width(32), .enable("false")) multiplexer_1 (
    .in0({32{1'b1}}), .in1(KBD_t), .out(KBD_in), .sel(KBD_AVAIL));
  Multiplexer #(.select(3), .width(32), .enable("false")) multiplexer_2 (
    .in0(ALU_Output), .in1(KBD_in), .in2(random), .in3(RAM), .in4(High), .in5(Low), .out(RF_Input),
    .sel(selector));  // open: in6, in7

  // Other names for the same wires on the sheet: ALU[31:0] = ALU_Output; clk = Clock
endmodule
