// Logisim project Little Endian to Big Endian.circ as structural Verilog: 1 circuit, main circuit Little Endian to Big Endian
module Little_Endian_to_Big_Endian (
  input  [31:0] LE,
  output [31:0] BE
);


  assign BE = {LE[7:0], LE[15:8], LE[23:16], LE[31:24]};
endmodule
