// Logisim project Negator.circ as structural Verilog: 1 circuit, main circuit Negator
module Negator (
  input  [31:0] Number,
  output [31:0] Output
);

  not not_1 (Output[0], Number[0]);
  not not_2 (Output[1], Number[1]);
  not not_3 (Output[2], Number[2]);
  not not_4 (Output[3], Number[3]);
  not not_5 (Output[4], Number[4]);
  not not_6 (Output[5], Number[5]);
  not not_7 (Output[6], Number[6]);
  not not_8 (Output[7], Number[7]);
  not not_9 (Output[8], Number[8]);
  not not_10 (Output[9], Number[9]);
  not not_11 (Output[10], Number[10]);
  not not_12 (Output[11], Number[11]);
  not not_13 (Output[12], Number[12]);
  not not_14 (Output[13], Number[13]);
  not not_15 (Output[14], Number[14]);
  not not_16 (Output[15], Number[15]);
  not not_17 (Output[16], Number[16]);
  not not_18 (Output[17], Number[17]);
  not not_19 (Output[18], Number[18]);
  not not_20 (Output[19], Number[19]);
  not not_21 (Output[20], Number[20]);
  not not_22 (Output[21], Number[21]);
  not not_23 (Output[22], Number[22]);
  not not_24 (Output[23], Number[23]);
  not not_25 (Output[24], Number[24]);
  not not_26 (Output[25], Number[25]);
  not not_27 (Output[26], Number[26]);
  not not_28 (Output[27], Number[27]);
  not not_29 (Output[28], Number[28]);
  not not_30 (Output[29], Number[29]);
  not not_31 (Output[30], Number[30]);
  not not_32 (Output[31], Number[31]);
endmodule
