// Logisim project PC.circ as structural Verilog: 1 circuit, main circuit PC
module PC (
  input  [31:0] Branch_Control,
  input  Enabled,
  input  Clock,
  input  Reset,
  output [31:0] Instruction
);

  Register #(.width(32)) PC (.D(Branch_Control), .en(Enabled), .Q(Instruction), .clk(Clock), .clr(Reset));
endmodule
