// Logisim project RAM Reader.circ as structural Verilog: 1 circuit, main circuit RAM Reader
module RAM_Reader (
  input  [31:0] O1,
  input  [31:0] O2,
  input  [31:0] O3,
  input  [31:0] O4,
  input  [31:0] Dir_ram,
  output [31:0] Ins_o_Val
);

  wire [31:0] multiplexer_1_out;

  Multiplexer #(.select(2), .width(32), .enable("false")) multiplexer_1 (
    .in0(O1), .in1(O2), .in2(O3), .in3(O4), .out(multiplexer_1_out), .sel(Dir_ram[3:2]));
  Little_Endian_to_Big_Endian little_endian_to_big_endian_1 (.LE(multiplexer_1_out), .BE(Ins_o_Val));

  // Other names for the same wires on the sheet: Mask[1:0] = Dir_ram[3:2]
endmodule
