// Logisim project Sig Div.circ as structural Verilog: 1 circuit, main circuit Sig DIV
module Sig_DIV (
  input  [31:0] A,
  input  [31:0] B,
  output [31:0] Low,
  output [31:0] High
);

  wire is_zero;
  wire [1:0] selector;
  wire [31:0] cte, minus_neg_division, minus_positive_division, multiplexer_1_out, multiplexer_2_out,
       neg_division, negator_3_out, negator_4_out, positive_division, rest, sig_mul_1_low;

  // Probe on A
  // Probe on B
  Negator #(.width(32)) negator_1 (.in(positive_division), .out(minus_positive_division));
  Adder #(.width(32)) adder_1 (.a(positive_division), .b(cte), .out(neg_division));  // open: cin, cout
  Negator #(.width(32)) negator_2 (.in(neg_division), .out(minus_neg_division));
  Comparator #(.width(1), .mode("unsigned")) comparator_1 (.a(1'b1), .b(A[31]), .eq(selector[1]));  // open: gt, lt
  Negator #(.width(32)) negator_3 (.in(A), .out(negator_3_out));
  Negator #(.width(32)) negator_4 (.in(B), .out(negator_4_out));
  Comparator #(.width(1)) comparator_2 (.a(B[31]), .b(1'b1), .eq(selector[0]));  // open: gt, lt
  Comparator #(.width(32)) comparator_3 (.a(rest), .b({32{1'b0}}), .eq(is_zero));  // open: gt, lt
  Multiplexer #(.width(32), .enable("false")) multiplexer_1 (
    .in0(A), .in1(negator_3_out), .out(multiplexer_1_out), .sel(selector[1]));
  Multiplexer #(.width(32), .enable("false")) multiplexer_2 (
    .in0(B), .in1(negator_4_out), .out(multiplexer_2_out), .sel(selector[0]));
  Divider #(.width(32)) divider_1 (
    .a(multiplexer_1_out), .b(multiplexer_2_out), .out(positive_division), .rem(rest));  // open: upper
  Multiplexer #(.width(32), .enable("false")) multiplexer_3 (.in0(32'h1), .in1({32{1'b0}}), .out(cte), .sel(is_zero));
  Sig_Mul sig_mul_1 (.A(B), .B(Low), .Low(sig_mul_1_low));  // open: High
  Multiplexer #(.select(2), .width(32), .enable("false")) multiplexer_4 (
    .in0(positive_division), .in1(minus_positive_division), .in2(minus_neg_division), .in3(neg_division),
    .out(Low), .sel(selector));
  Subtractor #(.width(32)) subtractor_1 (.a(A), .b(sig_mul_1_low), .out(High));  // open: bin, bout
  // Probe on Low
  // Probe on High

  // Other names for the same wires on the sheet: result[31:0] = Low; selectorB = selector[0]; selectorA = selector[1]
endmodule
