// Logisim project Sig Mul.circ as structural Verilog: 1 circuit, main circuit Sig Mul
module Sig_Mul (
  input  [31:0] A,
  input  [31:0] B,
  output [31:0] Low,
  output [31:0] High
);

  wire carry_low, NegOut, selectorA, selectorB;
  wire [31:0] adder_1_out, adder_2_out, multiplexer_1_out, multiplexer_2_out, multiplier_1_cout,
       multiplier_1_out, negator_1_out, negator_2_out, negator_3_output, negator_4_output;

  // Probe on A
  // Probe on B
  Comparator #(.width(1), .mode("unsigned")) comparator_1 (.a(1'b1), .b(A[31]), .eq(selectorA));  // open: gt, lt
  Negator #(.width(32)) negator_1 (.in(A), .out(negator_1_out));
  Negator #(.width(32)) negator_2 (.in(B), .out(negator_2_out));
  Comparator #(.width(1)) comparator_2 (.a(B[31]), .b(1'b1), .eq(selectorB));  // open: gt, lt
  Multiplexer #(.width(32), .enable("false")) multiplexer_1 (
    .in0(A), .in1(negator_1_out), .out(multiplexer_1_out), .sel(selectorA));
  Multiplexer #(.width(32), .enable("false")) multiplexer_2 (
    .in0(B), .in1(negator_2_out), .out(multiplexer_2_out), .sel(selectorB));
  Multiplier #(.width(32)) multiplier_1 (
    .a(multiplexer_1_out), .b(multiplexer_2_out), .out(multiplier_1_out), .cout(multiplier_1_cout));  // open: cin
  xor xor_1 (NegOut, selectorA, selectorB);
  Negator negator_3 (.Number(multiplier_1_out), .Output(negator_3_output));
  Negator negator_4 (.Number(multiplier_1_cout), .Output(negator_4_output));
  Adder #(.width(32)) adder_1 (.a(negator_3_output), .b(32'h1), .out(adder_1_out), .cout(carry_low));  // open: cin
  Adder #(.width(32)) adder_2 (.a(negator_4_output), .b({32{1'b0}}), .out(adder_2_out), .cin(carry_low));  // open: cout
  // Probe on Low
  Multiplexer #(.width(32), .enable("false")) multiplexer_3 (
    .in0(multiplier_1_out), .in1(adder_1_out), .out(Low), .sel(NegOut));
  Multiplexer #(.width(32), .enable("false")) multiplexer_4 (
    .in0(multiplier_1_cout), .in1(adder_2_out), .out(High), .sel(NegOut));
  // Probe on High
endmodule
