// Logisim project Write Ram.circ as structural Verilog: 1 circuit, main circuit Write Ram
module Write_Ram (
  input  [31:0] Dir_Ram,
  input  [31:0] Value,
  output [3:0] Mask,
  output [15:0] out_4,
  output [31:0] Bank_0,
  output [31:0] Bank_1,
  output [31:0] Bank_2,
  output [31:0] Bank_3
);

  wire [31:0] little_endian_to_big_endian_1_be;

  Little_Endian_to_Big_Endian little_endian_to_big_endian_1 (.LE(Value), .BE(little_endian_to_big_endian_1_be));
  Decoder #(.select(2), .enable("false")) decoder_1 (
    .out0(Mask[0]), .out1(Mask[1]), .out2(Mask[2]), .out3(Mask[3]), .sel(Dir_Ram[3:2]));
  Demultiplexer #(.select(2), .width(32), .enable("false")) demultiplexer_1 (
    .out0(Bank_0), .out1(Bank_1), .out2(Bank_2), .out3(Bank_3), .in(little_endian_to_big_endian_1_be),
    .sel(Dir_Ram[3:2]));

  assign out_4 = Dir_Ram[19:4];

  // Other names for the same wires on the sheet: Selector[1:0] = Dir_Ram[3:2]; Address[15:0] = Dir_Ram[19:4]
endmodule
